// Logisim project root.circ as structural Verilog: 7 circuits, main circuit main
module main (
);

  wire button_1_out, button_2_out, clk, controlpath_1_load, controlpath_1_store, datapath_1_progcontrol;
  wire [7:0] adder_1_out, datapath_1_datamemaddress, datapath_1_dataout, datapath_1_insaddress,
       multiplexer_1_out, ram_1_dout, register_1_q;
  wire [11:0] controlpath_1_sign;
  wire [23:0] rom_1_data;

  Clock clock_1 (.out(clk));
  Multiplexer #(.width(8)) multiplexer_1 (
    .in0(adder_1_out), .in1(datapath_1_insaddress), .out(multiplexer_1_out), .sel(datapath_1_progcontrol));
  Register register_1 (.D(multiplexer_1_out), .Q(register_1_q), .clk(clk), .clr(button_1_out));  // open: en
  Button button_1 (.out(button_1_out));
  Adder adder_1 (.a(register_1_q), .b(8'h1), .out(adder_1_out));  // open: cin, cout
  ROM #(.dataWidth(24)) rom_1 (.addr(register_1_q), .data(rom_1_data));
  DataPath datapath_1 (
    .Sign(controlpath_1_sign), .DataIn(ram_1_dout), .Params(rom_1_data[15:0]), .clk(clk),
    .DataOut(datapath_1_dataout), .InsAddress(datapath_1_insaddress),
    .DataMemAddress(datapath_1_datamemaddress), .ProgControl(datapath_1_progcontrol));
  ControlPath controlpath_1 (
    .Opcode(rom_1_data[23:16]), .Load(controlpath_1_load), .Store(controlpath_1_store),
    .Sign(controlpath_1_sign));
  RAM #(.asyncread("true"), .clearpin("true")) ram_1 (
    .addr(datapath_1_datamemaddress), .we(controlpath_1_store), .oe(controlpath_1_load), .clk(clk),
    .din(datapath_1_dataout), .dout(ram_1_dout), .clr(button_2_out));
  Button button_2 (.out(button_2_out));

  // Notes on the sheet:
  //   contents of rom_1 (hex, n*v repeats v):
  //   50003 50107 50200 a0300 504ff 30309 b0201 b0304 20005 70000 70101 70202 70303
endmodule

module ULA (
  input  [7:0] X,
  input  [7:0] Y,
  output ZeroReg,
  output [7:0] Z,
  output Carry
);

  ZeroChecker8bits zerochecker8bits_1 (.Checked(X), .ZeroFlag(ZeroReg));
  FullAdder8bits fulladder8bits_1 (.X(X), .Y(Y), .Cout(Carry), .Z(Z));  // open: Cin
endmodule

module ControlPath (
  input  [7:0] Opcode,
  output Load,
  output Store,
  output [11:0] Sign
);

  wire and_3_out, and_4_out, and_5_out, and_6_out, not_1_out, not_2_out, not_3_out, or_1_out, or_2_out,
       or_3_out, or_4_out;

  not not_1 (not_1_out, Opcode[3]);
  not not_2 (not_2_out, Opcode[2]);
  not not_3 (not_3_out, Opcode[1]);
  not not_4 (Load, Opcode[0]);
  and and_1 (Store, Opcode[1], Opcode[0], Opcode[2]);
  and and_2 (Sign[8], not_1_out, not_2_out, Opcode[1], Load);
  and and_3 (and_3_out, not_1_out, not_2_out, Opcode[1]);
  and and_4 (and_4_out, not_1_out, Opcode[2], not_3_out, Load);
  or or_1 (or_1_out, not_2_out, Opcode[0]);
  or or_2 (or_2_out, Opcode[2], Load);
  or or_3 (or_3_out, not_3_out, Opcode[0]);
  and and_5 (and_5_out, not_1_out, not_2_out);
  and and_6 (and_6_out, not_1_out, Opcode[1], Opcode[0]);
  or or_4 (or_4_out, Opcode[3], Opcode[0]);
  or or_5 (Sign[7], and_3_out, and_4_out);
  and and_7 (Sign[5], or_1_out, or_2_out);
  and and_8 (Sign[4], Opcode[3], or_3_out);
  or or_6 (Sign[3], and_5_out, and_6_out);
  and and_9 (Sign[0], Opcode[1], or_4_out);

  assign {Sign[11:9], Sign[6], Sign[2:1]} = {3'b000, Opcode[1:0], 1'b1};
endmodule

module DataPath (
  input  [11:0] Sign,
  input  [7:0] DataIn,
  input  [15:0] Params,
  input  clk,
  output [7:0] DataOut,
  output [7:0] InsAddress,
  output [7:0] DataMemAddress,
  output ProgControl
);

  wire and_1_out, decoder_1_out0, decoder_1_out1, decoder_1_out2, decoder_1_out3, decoder_1_out4,
       ula_1_zeroreg;
  wire [4:0] multiplexer_5_out, multiplexer_9_out, multiplexer_12_out;
  wire [7:0] Acc_q, Bacc_q, Carr_q, Datt_q, Extt_q, multiplexer_1_out, multiplexer_2_out, multiplexer_4_out,
       multiplexer_6_out, multiplexer_7_out, reg1Out, reg2Out, UlaOut;
  wire [7:5] multiplexer_9_out_2, multiplexer_12_out_2;

  Multiplexer #(.width(8)) multiplexer_1 (.in0(DataIn), .in1(Params[7:0]), .out(multiplexer_1_out), .sel(Sign[2]));
  Multiplexer #(.width(8)) multiplexer_2 (.in0(DataIn), .in1(Params[7:0]), .out(multiplexer_2_out), .sel(Sign[1]));
  Multiplexer #(.width(8)) multiplexer_3 (.in0(multiplexer_2_out), .in1(reg1Out), .out(DataOut), .sel(Sign[0]));
  Multiplexer #(.width(8)) multiplexer_4 (
    .in0(multiplexer_1_out), .in1(reg1Out), .out(multiplexer_4_out), .sel(Sign[0]));
  Multiplexer #(.width(5)) multiplexer_5 (.in0(Params[12:8]), .in1({5{1'b1}}), .out(multiplexer_5_out), .sel(Sign[3]));
  Decoder #(.enable("false"), .select(5)) decoder_1 (
    .out0(decoder_1_out0), .out1(decoder_1_out1), .out2(decoder_1_out2), .out3(decoder_1_out3),
    .out4(decoder_1_out4), .sel(multiplexer_5_out));  // open: out5, out6, out7, out8, out9, out10, out11, out12, out13, out14, out15, out16, out17, out18, out19, out20, out21, out22, out23, out24, out25, out26, out27, out28, out29, out30, out31
  Multiplexer #(.width(8)) multiplexer_6 (.in0(DataIn), .in1(reg2Out), .out(multiplexer_6_out), .sel(Sign[6]));
  Multiplexer #(.width(8)) multiplexer_7 (
    .in0(multiplexer_4_out), .in1(UlaOut), .out(multiplexer_7_out), .sel(Sign[4]));
  or or_1 (ProgControl, Sign[8], and_1_out);
  and and_1 (and_1_out, Sign[7], ula_1_zeroreg);
  Register Acc (.D(multiplexer_7_out), .en(decoder_1_out0), .Q(Acc_q), .clk(clk));  // open: clr
  Register Bacc (.D(multiplexer_7_out), .en(decoder_1_out1), .Q(Bacc_q), .clk(clk));  // open: clr
  Register Carr (.D(multiplexer_7_out), .en(decoder_1_out2), .Q(Carr_q), .clk(clk));  // open: clr
  Register Datt (.D(multiplexer_7_out), .en(decoder_1_out3), .Q(Datt_q), .clk(clk));  // open: clr
  Register Extt (.D(multiplexer_7_out), .en(decoder_1_out4), .Q(Extt_q), .clk(clk));  // open: clr
  ULA ula_1 (.X(reg1Out), .Y(multiplexer_6_out), .ZeroReg(ula_1_zeroreg), .Z(UlaOut));  // open: Carry
  Multiplexer #(.select(5), .width(8)) multiplexer_8 (
    .in0(Acc_q), .in1(Bacc_q), .in2(Carr_q), .in3(Datt_q), .in4(Extt_q), .out(reg1Out),
    .sel(multiplexer_9_out));  // open: in5, in6, in7, in8, in9, in10, in11, in12, in13, in14, in15, in16, in17, in18, in19, in20, in21, in22, in23, in24, in25, in26, in27, in28, in29, in30, in31
  Multiplexer #(.width(8)) multiplexer_9 (
    .in0(Params[15:8]), .in1(Params[7:0]), .out({multiplexer_9_out_2, multiplexer_9_out}), .sel(Sign[5]));
  Multiplexer #(.width(8)) multiplexer_10 (.in0(Params[7:0]), .in1(Params[15:8]), .out(DataMemAddress), .sel(Sign[5]));
  Multiplexer #(.select(5), .width(8)) multiplexer_11 (
    .in0(Acc_q), .in1(Bacc_q), .in2(Carr_q), .in3(Datt_q), .in4(Extt_q), .out(reg2Out),
    .sel(multiplexer_12_out));  // open: in5, in6, in7, in8, in9, in10, in11, in12, in13, in14, in15, in16, in17, in18, in19, in20, in21, in22, in23, in24, in25, in26, in27, in28, in29, in30, in31
  Multiplexer #(.width(8)) multiplexer_12 (
    .in0(Params[7:0]), .in1(Params[15:8]), .out({multiplexer_12_out_2, multiplexer_12_out}), .sel(Sign[5]));

  assign InsAddress = Params[7:0];

  // Other names for the same wires on the sheet: param2[7:0] = Params[7:0]; param1[7:0] = Params[15:8];
  //   selDataOut0 = Sign[0]; selDataIn1 = Sign[1]
endmodule

// Add8
module FullAdder8bits (
  input  [7:0] X,
  input  [7:0] Y,
  input  Cin,
  output [7:0] Z,
  output Cout
);

  wire fulladder1bit_1_cout, fulladder1bit_2_cout, fulladder1bit_3_cout, fulladder1bit_4_cout,
       fulladder1bit_5_cout, fulladder1bit_6_cout, fulladder1bit_7_cout;

  FullAdder1bit fulladder1bit_1 (.Cin(Cin), .X(X[0]), .Y(Y[0]), .Z(Z[0]), .Cout(fulladder1bit_1_cout));
  FullAdder1bit fulladder1bit_2 (.Cin(fulladder1bit_1_cout), .X(X[1]), .Y(Y[1]), .Z(Z[1]), .Cout(fulladder1bit_2_cout));
  FullAdder1bit fulladder1bit_3 (.Cin(fulladder1bit_2_cout), .X(X[2]), .Y(Y[2]), .Z(Z[2]), .Cout(fulladder1bit_3_cout));
  FullAdder1bit fulladder1bit_4 (.Cin(fulladder1bit_3_cout), .X(X[3]), .Y(Y[3]), .Z(Z[3]), .Cout(fulladder1bit_4_cout));
  FullAdder1bit fulladder1bit_5 (.Cin(fulladder1bit_4_cout), .X(X[4]), .Y(Y[4]), .Z(Z[4]), .Cout(fulladder1bit_5_cout));
  FullAdder1bit fulladder1bit_6 (.Cin(fulladder1bit_5_cout), .X(X[5]), .Y(Y[5]), .Z(Z[5]), .Cout(fulladder1bit_6_cout));
  FullAdder1bit fulladder1bit_7 (.Cin(fulladder1bit_6_cout), .X(X[6]), .Y(Y[6]), .Z(Z[6]), .Cout(fulladder1bit_7_cout));
  FullAdder1bit fulladder1bit_8 (.Cin(fulladder1bit_7_cout), .X(X[7]), .Y(Y[7]), .Z(Z[7]), .Cout(Cout));
endmodule

// Add1
module FullAdder1bit (
  input  X,
  input  Y,
  input  Cin,
  output Z,
  output Cout
);

  wire and_1_out, and_2_out, and_3_out, and_4_out, and_5_out, and_6_out, and_7_out, not_1_out, not_2_out,
       not_3_out;

  not not_1 (not_1_out, X);
  not not_2 (not_2_out, Y);
  not not_3 (not_3_out, Cin);
  and and_1 (and_1_out, not_1_out, not_2_out, Cin);
  and and_2 (and_2_out, not_1_out, Y, not_3_out);
  and and_3 (and_3_out, X, not_2_out, not_3_out);
  and and_4 (and_4_out, X, Y, Cin);
  and and_5 (and_5_out, Y, Cin);
  and and_6 (and_6_out, X, Cin);
  and and_7 (and_7_out, X, Y);
  or or_1 (Z, and_1_out, and_2_out, and_3_out, and_4_out);
  or or_2 (Cout, and_5_out, and_6_out, and_7_out);
endmodule

module ZeroChecker8bits (
  input  [7:0] Checked,
  output ZeroFlag
);

  wire not_1_out, not_2_out, not_3_out, not_4_out, not_5_out, not_6_out, not_7_out, not_8_out;

  not not_1 (not_1_out, Checked[7]);
  not not_2 (not_2_out, Checked[6]);
  not not_3 (not_3_out, Checked[5]);
  not not_4 (not_4_out, Checked[4]);
  not not_5 (not_5_out, Checked[3]);
  not not_6 (not_6_out, Checked[2]);
  not not_7 (not_7_out, Checked[1]);
  not not_8 (not_8_out, Checked[0]);
  and and_1 (ZeroFlag, not_1_out, not_2_out, not_3_out, not_4_out, not_5_out, not_6_out, not_7_out, not_8_out);
endmodule
